// Digital circuit 1mulit.dig as structural Verilog
module _1mulit (
  input  B0,
  input  B1,
  input  B2,
  input  B3,
  input  A2,
  input  A3,
  input  A0,
  input  A1,
  output [7:0] P
);

  wire and_2_out, and_5_out, and_6_out, and_7_out, and_9_out, and_12_out, and_13_out, and_15_out,
       fulladder_1_p1, fulladder_1_p2, fulladder_1_p4, fulladder_2_p1, fulladder_2_p2, fulladder_2_p4,
       fulladder_2_p5, fulladder_3_p1, fulladder_3_p4, fulladder_4_p4, fulladder_4_p5, fulladder_5_p1,
       fulladder_5_p5, fulladder_6_p1, fulladder_7_p1, fulladder_7_p4, fulladder_7_p5, fulladder_8_p1,
       fulladder_8_p4, fulladder_8_p5, fulladder_9_p4, fulladder_10_p1, fulladder_10_p5, fulladder_11_p4;

  // FullAdder fulladder_1: pin names not known; wires that end beside it: fulladder_1_p1, fulladder_1_p2, P[7], fulladder_1_p4, P[6]
  and and_1 (fulladder_1_p4, A3, B3);
  // FullAdder fulladder_2: pin names not known; wires that end beside it: fulladder_2_p1, fulladder_2_p2, fulladder_1_p2, fulladder_2_p4, fulladder_2_p5
  // FullAdder fulladder_3: pin names not known; wires that end beside it: fulladder_3_p1, fulladder_2_p5, fulladder_1_p1, fulladder_3_p4, P[5]
  and and_2 (and_2_out, A3, B1);
  // FullAdder fulladder_4: pin names not known; wires that end beside it: 1'b0, and_2_out, fulladder_2_p2, fulladder_4_p4, fulladder_4_p5
  and and_3 (fulladder_2_p4, A3, B2);
  and and_4 (fulladder_3_p4, A2, B3);
  and and_5 (and_5_out, A2, B2);
  // FullAdder fulladder_5: pin names not known; wires that end beside it: fulladder_5_p1, fulladder_4_p5, fulladder_2_p1, and_5_out, fulladder_5_p5
  and and_6 (and_6_out, A1, B3);
  // FullAdder fulladder_6: pin names not known; wires that end beside it: fulladder_6_p1, fulladder_5_p5, fulladder_3_p1, and_6_out, P[4]
  and and_7 (and_7_out, A2, B1);
  // FullAdder fulladder_7: pin names not known; wires that end beside it: fulladder_7_p1, and_7_out, fulladder_4_p4, fulladder_7_p4, fulladder_7_p5
  // FullAdder fulladder_8: pin names not known; wires that end beside it: fulladder_8_p1, fulladder_7_p5, fulladder_5_p1, fulladder_8_p4, fulladder_8_p5
  // FullAdder fulladder_9: pin names not known; wires that end beside it: 1'b0, fulladder_8_p5, fulladder_6_p1, fulladder_9_p4, P[3]
  and and_8 (fulladder_7_p4, A3, B0);
  and and_9 (and_9_out, A1, B1);
  and and_10 (fulladder_8_p4, A1, B2);
  and and_11 (fulladder_9_p4, A0, B3);
  and and_12 (and_12_out, A2, B0);
  // FullAdder fulladder_10: pin names not known; wires that end beside it: fulladder_10_p1, and_9_out, fulladder_7_p1, and_12_out, fulladder_10_p5
  // FullAdder fulladder_11: pin names not known; wires that end beside it: 1'b0, fulladder_10_p5, fulladder_8_p1, fulladder_11_p4, P[2]
  and and_13 (and_13_out, A0, B1);
  and and_14 (fulladder_11_p4, A0, B2);
  and and_15 (and_15_out, A1, B0);
  // FullAdder fulladder_12: pin names not known; wires that end beside it: 1'b0, and_13_out, fulladder_10_p1, and_15_out, P[1]
  and and_16 (P[0], A0, B0);

  // Other names for the same wires on the sheet: A_0 = A0; A_1 = A1; A_2 = A2; A_3 = A3; P_0 = P[0]; P_1 = P[1];
  //   P_2 = P[2]; P_3 = P[3]; P_4 = P[4]; P_5 = P[5]; P_6 = P[6]; P_7 = P[7]
endmodule
